// Logisim project MIPS32.circ as structural Verilog: 10 circuits, main circuit main
module main (
  input  in_1,
  input  in_2,
  input  in_3,
  input  [1:0] in_4,
  input  [1:0] in_5,
  input  [1:0] in_6,
  input  [1:0] in_7,
  input  [1:0] in_8,
  output out_9,
  output [1:0] out_10
);

  Multiplexer #(.enable("false")) multiplexer_1 (.in0(in_1), .in1(in_2), .out(out_9), .sel(in_3));
  Multiplexer #(.select(2), .width(2), .enable("false")) multiplexer_2 (
    .in0(in_4), .in1(in_5), .in2(in_6), .in3(in_7), .out(out_10), .sel(in_8));
endmodule

module MIPS32 (
);

  wire and_1_out, and_2_out, and_3_out, c1_out, Choose2, maincontrol_1_signextend, MemToReg, or_1_out, Q,
       RegWrite, ShiftLocat, XMMemToReg, XMRegW;
  wire [1:0] Choose10, EXCtrl_q, ForwA, ForwB, maincontrol_1_memtoreg, maincontrol_1_regdest, PC_q,
       WBCtrl0_q_2;
  wire [1:1] WBCtrl0_q;
  wire [2:0] maincontrol_1_memread, MEMCtrl0_q;
  wire [3:0] ALUOP;
  wire [4:0] multiplexer_3_out, Rd_q, RegDest, Rs_q, Rt_q, SA, Sa_q, XMRd;
  wire [7:0] alucontrol_1_shiftlocat;
  wire [29:0] incrementer_1_p2, PC_q_2;
  wire [31:0] A_q, ALUresult1_q, B_q, bit_extender_1_out, bit_extender_2_out, DetectB_Table, Imm_q,
       lui_1_outp, MEMdata_q, mips_alu_1_p5, mipsprogramrom_1_p2, movz_1_outp, multiplexer_1_out,
       multiplexer_2_out, multiplexer_5_out, multiplexer_6_out, multiplexer_7_out, multiplexer_9_out,
       Original_Instr, PC4DE_q, PC4EM_q, PC4FD_q, registerfile_1_p7, registerfile_1_p8, slt_1_sioupt,
       slt_1_unoutp, WBdata, XMALU;

  Clock c1 (.out(c1_out));
  Register #(.width(32)) PC (.D({incrementer_1_p2, PC_q}), .clk(c1_out), .Q({PC_q_2, PC_q}));  // open: en, clr
  // Incrementer #(.width(30)) incrementer_1: pin names not known; wires that end beside it: PC_q_2, incrementer_1_p2
  // MIPSProgramROM mipsprogramrom_1: pin names not known; wires that end beside it: {PC_q_2, PC_q}, mipsprogramrom_1_p2
  Register #(.width(32)) PC4FD (.D({incrementer_1_p2, PC_q}), .clk(c1_out), .Q(PC4FD_q));  // open: en, clr
  Register #(.width(32)) Instruction (.D(mipsprogramrom_1_p2), .clk(c1_out), .Q(Original_Instr));  // open: en, clr
  Detect_B_Instr detect_b_instr_1 (.Origin_Instr(Original_Instr), .Out_Instr(DetectB_Table));
  // RegisterFile #(.trigger("falling")) registerfile_1: pin names not known; wires that end beside it: WBdata, c1_out, RegWrite, RegDest, DetectB_Table[25:21], DetectB_Table[20:16], registerfile_1_p7, registerfile_1_p8
  assign bit_extender_1_out = {{16{1'b0}}, DetectB_Table[15:0]};  // Bit_Extender bit_extender_1
  Multiplexer #(.width(32), .enable("false")) multiplexer_1 (
    .in0(bit_extender_1_out), .in1(bit_extender_2_out), .out(multiplexer_1_out),
    .sel(maincontrol_1_signextend));
  assign bit_extender_2_out = {{16{DetectB_Table[15]}}, DetectB_Table[15:0]};  // Bit_Extender bit_extender_2
  ALUControl alucontrol_1 (
    .OP5(DetectB_Table[31]), .OP4(DetectB_Table[30]), .OP3(DetectB_Table[29]), .OP2(DetectB_Table[28]),
    .OP1(DetectB_Table[27]), .OP0(DetectB_Table[26]), .FUNC5(DetectB_Table[5]), .FUNC4(DetectB_Table[4]),
    .FUNC3(DetectB_Table[3]), .FUNC2(DetectB_Table[2]), .FUNC1(DetectB_Table[1]), .FUNC0(DetectB_Table[0]),
    .ALUOP3(alucontrol_1_shiftlocat[7]), .ALUOP2(alucontrol_1_shiftlocat[6]),
    .ALUOP1(alucontrol_1_shiftlocat[5]), .ALUOP0(alucontrol_1_shiftlocat[4]),
    .Choose2(alucontrol_1_shiftlocat[3]), .Choose1(alucontrol_1_shiftlocat[2]),
    .Choose0(alucontrol_1_shiftlocat[1]), .ShiftLocat(alucontrol_1_shiftlocat[0]));
  MainControl maincontrol_1 (
    .OP5(DetectB_Table[31]), .OP4(DetectB_Table[30]), .OP3(DetectB_Table[29]), .OP2(DetectB_Table[28]),
    .OP1(DetectB_Table[27]), .OP0(DetectB_Table[26]), .SignExtend(maincontrol_1_signextend),
    .RegDest(maincontrol_1_regdest[0]), .ALUsrc(maincontrol_1_regdest[1]),
    .MemRead(maincontrol_1_memread[0]), .MemW(maincontrol_1_memread[1]), .Branch(maincontrol_1_memread[2]),
    .MemToReg(maincontrol_1_memtoreg[0]), .RegWr(maincontrol_1_memtoreg[1]));
  Register #(.width(32)) PC4DE (.D(PC4FD_q), .clk(c1_out), .Q(PC4DE_q));  // open: en, clr
  Register #(.width(32)) A (.D(registerfile_1_p7), .clk(c1_out), .Q(A_q));  // open: en, clr
  Register #(.width(32)) B (.D(registerfile_1_p8), .clk(c1_out), .Q(B_q));  // open: en, clr
  Register #(.width(32)) Imm (.D(multiplexer_1_out), .clk(c1_out), .Q(Imm_q));  // open: en, clr
  Register #(.width(5)) Rd (.D(DetectB_Table[15:11]), .clk(c1_out), .Q(Rd_q));  // open: en, clr
  Register #(.width(5)) Rt (.D(DetectB_Table[20:16]), .clk(c1_out), .Q(Rt_q));  // open: en, clr
  Register #(.width(5)) Rs (.D(DetectB_Table[25:21]), .Q(Rs_q));  // open: en, clk, clr
  Register #(.width(5)) u_Sa (.D(DetectB_Table[10:6]), .Q(Sa_q));  // open: en, clk, clr
  Register ALUCtrl (.D(alucontrol_1_shiftlocat), .Q({ALUOP, Choose2, Choose10, ShiftLocat}));  // open: en, clk, clr
  Register #(.width(2)) EXCtrl (.D(maincontrol_1_regdest), .clk(c1_out), .Q(EXCtrl_q));  // open: en, clr
  Register #(.width(3)) MEMCtrl0 (.D(maincontrol_1_memread), .clk(c1_out), .Q(MEMCtrl0_q));  // open: en, clr
  Register #(.width(2)) WBCtrl0 (
    .D(maincontrol_1_memtoreg), .clk(c1_out), .Q({WBCtrl0_q[1], WBCtrl0_q_2[0]}));  // open: en, clr
  Multiplexer #(.width(32), .enable("false")) multiplexer_2 (
    .in0(B_q), .in1(Imm_q), .out(multiplexer_2_out), .sel(EXCtrl_q[1]));
  Multiplexer #(.width(5), .enable("false")) multiplexer_3 (
    .in0(Rt_q), .in1(Rd_q), .out(multiplexer_3_out), .sel(EXCtrl_q[0]));
  Multiplexer #(.width(5), .enable("false")) multiplexer_4 (.in0(Rs_q), .in1(Sa_q), .out(SA), .sel(ShiftLocat));
  Multiplexer #(.select(2), .width(32), .enable("false")) multiplexer_5 (
    .in0(A_q), .in1(WBdata), .in3(XMALU), .out(multiplexer_5_out), .sel(ForwA));  // open: in2
  Multiplexer #(.select(2), .width(32), .enable("false")) multiplexer_6 (
    .in0(multiplexer_2_out), .in1(WBdata), .in2(XMALU), .out(multiplexer_6_out), .sel(ForwB));  // open: in3
  // Mips_ALU mips_alu_1: pin names not known; wires that end beside it: multiplexer_5_out, multiplexer_6_out, ALUOP, SA, mips_alu_1_p5
  SLT slt_1 (.A(A_q), .B(multiplexer_2_out), .UnOutp(slt_1_unoutp), .SiOupt(slt_1_sioupt));
  LUI lui_1 (.B(multiplexer_2_out), .Outp(lui_1_outp));
  and and_1 (and_1_out, ~Choose2, Q);  // AND_Gate
  and and_2 (and_2_out, ~Q, Choose2);  // AND_Gate
  and and_3 (and_3_out, Choose10[0], Choose10[1]);
  Multiplexer #(.width(32), .enable("false")) multiplexer_7 (
    .in0(slt_1_unoutp), .in1(slt_1_sioupt), .out(multiplexer_7_out), .sel(Choose2));
  MOVZ movz_1 (.rt(Rt_q), .rs_A(A_q), .Outp(movz_1_outp), .RegWr_Q(Q));
  or or_1 (or_1_out, and_1_out, and_2_out);
  Multiplexer #(.enable("false")) multiplexer_8 (
    .in0(WBCtrl0_q[1]), .in1(or_1_out), .out(WBCtrl0_q_2[1]), .sel(and_3_out));
  Multiplexer #(.select(2), .width(32), .enable("false")) multiplexer_9 (
    .in0(mips_alu_1_p5), .in1(multiplexer_7_out), .in2(lui_1_outp), .in3(movz_1_outp),
    .out(multiplexer_9_out), .sel(Choose10));
  ForwardingUnit forwardingunit_1 (
    .XMRegW(XMRegW), .XMRd(XMRd), .DXRs(Rt_q), .DXRt(Rd_q), .MWRegW(RegWrite), .MWRd(RegDest),
    .ForwardA(ForwA), .ForwardB(ForwB));
  Register #(.width(32)) PC4EM (.D(PC4DE_q), .clk(c1_out), .Q(PC4EM_q));  // open: en, clr
  Register #(.width(32)) ALUresultD (.D(multiplexer_9_out), .clk(c1_out), .Q(XMALU));  // open: en, clr
  Register #(.width(32)) Bdata (.D(B_q));  // open: en, clk, Q, clr
  Register #(.width(5)) Dest0 (.D(multiplexer_3_out), .clk(c1_out), .Q(XMRd));  // open: en, clr
  Register #(.width(3)) MEMCtrl1 (.D(MEMCtrl0_q), .clk(c1_out));  // open: en, Q, clr
  Register #(.width(2)) WBCtrl1 (.D(WBCtrl0_q_2), .clk(c1_out), .Q({XMRegW, XMMemToReg}));  // open: en, clr
  // MIPS_RAM mips_ram_1: pin names not known
  Register #(.width(32)) Target (.D(PC4EM_q), .clk(c1_out));  // open: en, Q, clr
  Register #(.width(32)) ALUresult1 (.D(XMALU), .clk(c1_out), .Q(ALUresult1_q));  // open: en, clr
  Register #(.width(32)) MEMdata (.clk(c1_out), .Q(MEMdata_q));  // open: D, en, clr
  Register #(.width(5)) Dest1 (.D(XMRd), .clk(c1_out), .Q(RegDest));  // open: en, clr
  Register #(.width(2)) WBCtrl2 (.D({XMRegW, XMMemToReg}), .clk(c1_out), .Q({RegWrite, MemToReg}));  // open: en, clr
  Multiplexer #(.width(32), .enable("false")) multiplexer_10 (
    .in0(ALUresult1_q), .in1(MEMdata_q), .out(WBdata), .sel(MemToReg));

  // Notes on the sheet:
  //   IF stage
  //   IF/ID
  //   ID stage
  //   ID/EX
  //   EX stage
  //   EX/MEM
  //   MEM stage
  //   MEM/WB
  //   WB stage
endmodule

module MainControl (
  input  OP5,
  input  OP4,
  input  OP3,
  input  OP2,
  input  OP1,
  input  OP0,
  output SignExtend,
  output RegDest,
  output ALUsrc,
  output MemRead,
  output MemW,
  output Branch,
  output MemToReg,
  output RegWr
);

  wire and_5_out, and_6_out, and_7_out, not_2_out, not_3_out, not_4_out, not_5_out, not_6_out, not_7_out,
       not_8_out, not_9_out, not_10_out;

  not not_1 (SignExtend, OP2);
  not not_2 (not_2_out, OP5);
  not not_3 (not_3_out, OP3);
  or or_1 (ALUsrc, OP3, OP5);
  not not_4 (not_4_out, OP3);
  and and_1 (MemW, OP5, OP3);
  not not_5 (not_5_out, OP5);
  not not_6 (not_6_out, OP3);
  not not_7 (not_7_out, OP3);
  not not_8 (not_8_out, OP2);
  not not_9 (not_9_out, OP5);
  not not_10 (not_10_out, OP3);
  and and_2 (RegDest, not_2_out, not_3_out);
  and and_3 (MemRead, OP5, not_4_out);
  and and_4 (Branch, not_5_out, not_6_out, OP2);
  and and_5 (and_5_out, not_7_out, not_8_out);
  and and_6 (and_6_out, not_9_out, OP3);
  and and_7 (and_7_out, OP5, not_10_out);
  or or_2 (RegWr, and_5_out, and_6_out, and_7_out);

  assign MemToReg = OP5;
endmodule

module LUI (
  input  [31:0] B,
  output [31:0] Outp
);


  assign Outp = {B[15:0], B[31:16]};
endmodule

module MOVZ (
  input  [4:0] rt,
  input  [31:0] rs_A,
  output [31:0] Outp,
  output RegWr_Q
);

  wire [4:0] not_1_out;

  assign not_1_out = ~rt;  // NOT_Gate not_1, 5 bits wide
  and and_1 (RegWr_Q, not_1_out[0], not_1_out[1], not_1_out[2], not_1_out[3], not_1_out[4]);

  assign Outp = rs_A;
endmodule

module ALUControl (
  input  OP5,
  input  OP4,
  input  OP3,
  input  OP2,
  input  OP1,
  input  OP0,
  input  FUNC5,
  input  FUNC4,
  input  FUNC3,
  input  FUNC2,
  input  FUNC1,
  input  FUNC0,
  output ALUOP3,
  output ALUOP2,
  output ALUOP1,
  output ALUOP0,
  output Choose2,
  output Choose1,
  output Choose0,
  output ShiftLocat
);

  wire and_2_out, and_3_out, and_4_out, and_5_out, and_6_out, and_7_out, and_8_out, and_9_out, and_10_out,
       and_11_out, and_12_out, and_13_out, and_14_out, not_1_out, not_2_out, not_3_out, not_4_out, not_5_out,
       not_6_out, not_7_out, not_8_out, not_9_out, not_10_out, not_11_out, not_12_out, not_13_out,
       not_14_out, not_15_out, not_16_out, not_17_out, not_18_out, not_19_out, not_20_out, not_21_out,
       not_22_out, not_23_out, not_24_out, not_25_out, not_26_out, not_27_out;

  not not_1 (not_1_out, OP0);
  not not_2 (not_2_out, FUNC5);
  not not_3 (not_3_out, FUNC3);
  not not_4 (not_4_out, FUNC0);
  not not_5 (not_5_out, OP3);
  not not_6 (not_6_out, OP1);
  not not_7 (not_7_out, OP3);
  and and_1 (ALUOP2, not_7_out, FUNC1);
  and and_2 (and_2_out, FUNC5, FUNC0);
  not not_8 (not_8_out, OP3);
  and and_3 (and_3_out, not_8_out, not_9_out, FUNC0);
  not not_9 (not_9_out, FUNC5);
  not not_10 (not_10_out, OP3);
  not not_11 (not_11_out, FUNC5);
  not not_12 (not_12_out, OP5);
  not not_13 (not_13_out, OP4);
  not not_14 (not_14_out, OP3);
  not not_15 (not_15_out, OP2);
  not not_16 (not_16_out, OP1);
  not not_17 (not_17_out, OP0);
  not not_18 (not_18_out, FUNC4);
  not not_19 (not_19_out, FUNC2);
  not not_20 (not_20_out, OP5);
  not not_21 (not_21_out, OP4);
  not not_22 (not_22_out, OP2);
  not not_23 (not_23_out, OP0);
  not not_24 (not_24_out, OP3);
  and and_4 (and_4_out, not_24_out, not_25_out, FUNC3);
  not not_25 (not_25_out, FUNC5);
  and and_5 (and_5_out, OP2, OP1, OP0);
  not not_26 (not_26_out, OP3);
  and and_6 (and_6_out, not_26_out, FUNC3);
  not not_27 (not_27_out, OP2);
  and and_7 (and_7_out, not_27_out, OP1);
  not not_28 (ShiftLocat, FUNC2);
  and and_8 (and_8_out, not_1_out, not_2_out, FUNC4, not_3_out, FUNC2, FUNC1, not_4_out);
  and and_9 (and_9_out, not_5_out, FUNC5, FUNC2);
  and and_10 (and_10_out, OP2, not_6_out);
  and and_11 (and_11_out, OP2, OP0);
  or or_1 (ALUOP1, and_2_out, OP0, OP1);
  or or_2 (ALUOP0, and_3_out, OP1);
  and and_12 (and_12_out, not_10_out, not_11_out, FUNC3, FUNC0);
  and and_13 (and_13_out, not_12_out, not_13_out, not_14_out, not_15_out, not_16_out, not_17_out, not_18_out, FUNC3, not_19_out, FUNC1, FUNC0);
  and and_14 (and_14_out, not_20_out, not_21_out, OP3, not_22_out, OP1, not_23_out);
  or or_3 (Choose1, and_4_out, and_5_out);
  or or_4 (Choose0, and_6_out, and_7_out);
  or or_5 (ALUOP3, and_8_out, and_9_out, and_10_out, and_11_out);
  or or_6 (Choose2, and_12_out, and_13_out, and_14_out);
endmodule

module SLT (
  input  [31:0] A,
  input  [31:0] B,
  output [31:0] UnOutp,
  output [31:0] SiOupt
);

  wire comparator_1_lt, comparator_2_lt;

  Comparator #(.width(32), .mode("unsigned")) comparator_1 (.a(A), .b(B), .lt(comparator_1_lt));  // open: gt, eq
  Comparator #(.width(32)) comparator_2 (.a(A), .b(B), .lt(comparator_2_lt));  // open: gt, eq
  assign UnOutp = {{31{1'b0}}, comparator_1_lt};  // Bit_Extender bit_extender_1
  assign SiOupt = {{31{1'b0}}, comparator_2_lt};  // Bit_Extender bit_extender_2

  // Notes on the sheet:
  //   Unsigned_A<B?
  //   Signed_A<B?
endmodule

module Detect_B_Instr (
  input  [31:0] Origin_Instr,
  output [31:0] Out_Instr
);


  assign Out_Instr = Origin_Instr;
endmodule

module ForwardingChoose (
  input  case1,
  input  case2,
  input  case3,
  input  case4,
  output A1,
  output A0,
  output B1,
  output B0
);

  wire not_1_out, not_2_out;

  not not_1 (not_1_out, case1);
  and and_1 (A0, not_1_out, case3);
  not not_2 (not_2_out, case2);
  and and_2 (B0, not_2_out, case4);

  assign A1 = case1;
  assign B1 = case2;
endmodule

module ForwardingUnit (
  input  XMRegW,
  input  [4:0] XMRd,
  input  [4:0] DXRs,
  input  [4:0] DXRt,
  input  MWRegW,
  input  [4:0] MWRd,
  output [1:0] ForwardA,
  output [1:0] ForwardB
);

  wire and_1_out, and_2_out, and_3_out, and_4_out, and_5_out, and_6_out, nor_1_out, nor_2_out, nor_3_out,
       nor_4_out, not_1_out, not_2_out, or_1_out, or_2_out;
  wire [4:0] xor_1_out, xor_2_out, xor_3_out, xor_4_out;

  or or_1 (or_1_out, XMRd[0], XMRd[1], XMRd[2], XMRd[3], XMRd[4]);
  assign xor_1_out = XMRd ^ DXRs;  // XOR_Gate xor_1, 5 bits wide
  assign xor_2_out = XMRd ^ DXRt;  // XOR_Gate xor_2, 5 bits wide
  assign xor_3_out = DXRs ^ MWRd;  // XOR_Gate xor_3, 5 bits wide
  assign xor_4_out = DXRt ^ MWRd;  // XOR_Gate xor_4, 5 bits wide
  nor nor_1 (nor_1_out, xor_1_out[0], xor_1_out[1], xor_1_out[2], xor_1_out[3], xor_1_out[4]);
  nor nor_2 (nor_2_out, xor_2_out[0], xor_2_out[1], xor_2_out[2], xor_2_out[3], xor_2_out[4]);
  nor nor_3 (nor_3_out, xor_3_out[0], xor_3_out[1], xor_3_out[2], xor_3_out[3], xor_3_out[4]);
  or or_2 (or_2_out, MWRd[0], MWRd[1], MWRd[2], MWRd[3], MWRd[4]);
  nor nor_4 (nor_4_out, xor_4_out[0], xor_4_out[1], xor_4_out[2], xor_4_out[3], xor_4_out[4]);
  and and_1 (and_1_out, XMRegW, or_1_out, nor_1_out);
  and and_2 (and_2_out, XMRegW, or_1_out, nor_2_out);
  not not_1 (not_1_out, and_1_out);
  not not_2 (not_2_out, and_2_out);
  and and_3 (and_3_out, XMRegW, or_1_out, nor_1_out);
  and and_4 (and_4_out, XMRegW, or_1_out, nor_2_out);
  and and_5 (and_5_out, nor_3_out, not_1_out, MWRegW, or_2_out);
  and and_6 (and_6_out, nor_4_out, not_2_out, or_2_out, MWRegW);
  ForwardingChoose forwardingchoose_1 (
    .case1(and_3_out), .case2(and_4_out), .case3(and_5_out), .case4(and_6_out), .A1(ForwardA[1]),
    .A0(ForwardA[0]), .B1(ForwardB[1]), .B0(ForwardB[0]));

  // Notes on the sheet:
  //   EX Hazard 1
  //   EX Hazard 2
  //   MEM 1
  //   MEM 2
endmodule
