// Logisim project MIPS32.circ as structural Verilog: 18 circuits, main circuit main
module main (
  input  in_1,
  input  in_2,
  input  in_3,
  input  [1:0] in_4,
  input  [1:0] in_5,
  input  [1:0] in_6,
  input  [1:0] in_7,
  input  [1:0] in_8,
  output out_9,
  output [1:0] out_10
);

  Multiplexer #(.enable("false")) multiplexer_1 (.in0(in_1), .in1(in_2), .out(out_9), .sel(in_3));
  Multiplexer #(.select(2), .width(2), .enable("false")) multiplexer_2 (
    .in0(in_4), .in1(in_5), .in2(in_6), .in3(in_7), .out(out_10), .sel(in_8));
endmodule

module MIPS32 (
);

  wire and_1_out, and_2_out, and_3_out, and_4_out, and_5_out, and_6_out, and_7_out, and_8_out, Branch,
       c1_out, Choose2, is_zero_1_is_zero, JR, Jump, LUH, maincontrol_1_signextend, MemToReg,
       multiplexer_29_out, multiplexer_30_out, not_1_out, not_2_out, not_3_out, not_4_out, not_5_out,
       not_6_out, not_7_out, not_8_out, not_9_out, not_10_out, not_11_out, not_12_out, not_13_out,
       not_14_out, not_15_out, not_16_out, not_17_out, not_18_out, not_19_out, not_20_out, not_21_out,
       not_22_out, not_23_out, or_1_out, or_2_out, pcctrldecode_1_jal, pcctrldecode_1_jal_jalr, Q,
       RAM_or_not_q, RegWrite, RI, ShiftLocat, Use_RAM, XMMemToReg, XMRegW;
  wire [1:0] bit_extender_14_out, bit_extender_16_out, Choose10, EXCtrl_q, ForwA, ForwB,
       maincontrol_1_memtoreg, maincontrol_1_regdest, multiplexer_18_out, multiplexer_20_out, PC_q, WBCtrl0_q;
  wire [1:1] multiplexer_32_out, PCsel;
  wire [2:0] bit_extender_15_out, Load_Store_EX_q, maincontrol_1_memread, MEMCtrl0_q, multiplexer_19_out;
  wire [3:0] ALUOP, bit_extender_17_out, bit_extender_20_out, decoder_1_out0, Load_Store_MEM_q,
       load_storecontrol_1_ls0, multiplexer_21_out, multiplexer_35_out;
  wire [4:0] bit_extender_9_out, bit_extender_10_out, bit_extender_11_out, bit_extender_12_out,
       bit_extender_18_out, DXRd, ID_Ra, ID_Rb, Instruction_q_3, Instruction_q_4, multiplexer_13_out,
       multiplexer_14_out, multiplexer_15_out, multiplexer_16_out, multiplexer_26_out, Rd_q, RegDest, Rs_q,
       Rt_q, SA, Sa_q, XMRd;
  wire [5:0] Instruction_q, Instruction_q_2;
  wire [7:0] alucontrol_1_shiftlocat, bit_extender_13_out, multiplexer_17_out, multiplexer_36_out;
  wire [25:0] PC4DE_q;
  wire [29:0] incrementer_1_p2, PC_q_2;
  wire [31:0] A_q, ALUresult1_q, B_q, bit_extender_1_out, bit_extender_2_out, bit_extender_3_out,
       bit_extender_4_out, bit_extender_5_out, bit_extender_6_out, bit_extender_7_out, bit_extender_8_out,
       bit_extender_19_out, bit_extender_21_out, bit_extender_22_out, calc_store_load_1_load_store_addr, FrA,
       FrB, Imm_q, Instr, LastIns, leftshift2_2_outp, lui_1_outp, MEM_B_q, MEMdata_q, mips_alu_1_p5,
       mips_ram_1_p7, mipsprogramrom_1_p2, movz_1_outp, multiplexer_1_out, multiplexer_2_out,
       multiplexer_3_out, multiplexer_4_out, multiplexer_5_out, multiplexer_6_out, multiplexer_7_out,
       multiplexer_8_out, multiplexer_9_out, multiplexer_10_out, multiplexer_11_out, multiplexer_12_out,
       multiplexer_24_out, multiplexer_27_out, multiplexer_28_out, multiplexer_33_out, multiplexer_34_out,
       multiplexer_37_out, multiplexer_38_out, PC_8, PCabs, PCabs_q, PCreg_q, PCrel, PCrel_q,
       registerfile_1_p7, registerfile_1_p8, slt_1_sioupt, slt_1_unoutp, undriven, WBdata, XMALU;
  wire [31:28] leftshift2_1_outp;

  Clock c1 (.out(c1_out));
  Multiplexer #(.width(32), .enable("false")) multiplexer_1 (
    .in0({incrementer_1_p2, PC_q}), .in1(PCrel), .out(multiplexer_1_out), .sel(Branch));
  Multiplexer #(.width(32), .enable("false")) multiplexer_2 (
    .in0(FrA), .in1(PCabs), .out(multiplexer_2_out), .sel(PCsel[1]));
  Register #(.width(32)) PC (.D(multiplexer_3_out), .clk(c1_out), .Q({PC_q_2, PC_q}));  // open: en, clr
  Multiplexer #(.width(32), .enable("false")) multiplexer_3 (
    .in0(multiplexer_4_out), .in1(LastIns), .out(multiplexer_3_out), .sel(LUH));
  Multiplexer #(.width(32), .enable("false")) multiplexer_4 (
    .in0(multiplexer_1_out), .in1(multiplexer_2_out), .out(multiplexer_4_out), .sel(Jump));
  assign bit_extender_1_out = {{31{1'b0}}, not_1_out};  // Bit_Extender bit_extender_1
  or or_1 (or_1_out, Branch, Jump);
  // Incrementer #(.width(30)) incrementer_1: pin names not known; wires that end beside it: PC_q_2, incrementer_1_p2
  // MIPSProgramROM mipsprogramrom_1: pin names not known; wires that end beside it: {PC_q_2, PC_q}, mipsprogramrom_1_p2
  Multiplexer #(.width(32), .enable("false")) multiplexer_5 (
    .in0(mipsprogramrom_1_p2), .in1(bit_extender_1_out), .out(multiplexer_5_out), .sel(or_1_out));
  not not_1 (not_1_out, or_1_out);
  Register #(.width(32)) Instruction (
    .D(multiplexer_6_out), .clk(c1_out),
    .Q({Instruction_q, ID_Ra, ID_Rb, Instruction_q_4, Instruction_q_3, Instruction_q_2}));  // open: en, clr
  Multiplexer #(.width(32), .enable("false")) multiplexer_6 (
    .in0(multiplexer_5_out),
    .in1({Instruction_q, ID_Ra, ID_Rb, Instruction_q_4, Instruction_q_3, Instruction_q_2}),
    .out(multiplexer_6_out), .sel(LUH));
  Register #(.width(32)) PC4FD (.D({incrementer_1_p2, PC_q}), .clk(c1_out), .Q(LastIns));  // open: en, clr
  // Probe on WBdata
  // Probe on RegWrite
  // Probe on RegDest
  Load_storeControl load_storecontrol_1 (
    .OP5(Instruction_q[5]), .OP4(Instruction_q[4]), .OP3(Instruction_q[3]), .OP2(Instruction_q[2]),
    .OP1(Instruction_q[1]), .OP0(Instruction_q[0]), .LS0(load_storecontrol_1_ls0[0]),
    .LS1(load_storecontrol_1_ls0[1]), .LS2(load_storecontrol_1_ls0[2]), .LS3(load_storecontrol_1_ls0[3]));
  assign bit_extender_2_out = {{31{1'b0}}, not_3_out};  // Bit_Extender bit_extender_2
  not not_2 (not_2_out, LUH);
  assign bit_extender_3_out = {{31{1'b0}}, not_2_out};  // Bit_Extender bit_extender_3
  and and_1 (and_1_out, Use_RAM, not_4_out);
  not not_3 (not_3_out, LUH);
  Multiplexer #(.width(32), .enable("false")) multiplexer_7 (
    .in0(LastIns), .in1(bit_extender_3_out), .out(multiplexer_7_out), .sel(LUH));
  // RegisterFile #(.trigger("falling")) registerfile_1: pin names not known; wires that end beside it: WBdata, c1_out, RegWrite, RegDest, ID_Ra, ID_Rb, registerfile_1_p7, registerfile_1_p8
  assign bit_extender_4_out = {{16{1'b0}}, {Instruction_q_4, Instruction_q_3, Instruction_q_2}};  // Bit_Extender bit_extender_4
  Multiplexer #(.width(32), .enable("false")) multiplexer_8 (
    .in0(bit_extender_4_out), .in1(bit_extender_5_out), .out(multiplexer_8_out),
    .sel(maincontrol_1_signextend));
  assign bit_extender_5_out = {{16{Instruction_q_4[4]}}, {Instruction_q_4, Instruction_q_3, Instruction_q_2}};  // Bit_Extender bit_extender_5
  ALUControl alucontrol_1 (
    .OP5(Instruction_q[5]), .OP4(Instruction_q[4]), .OP3(Instruction_q[3]), .OP2(Instruction_q[2]),
    .OP1(Instruction_q[1]), .OP0(Instruction_q[0]), .FUNC5(Instruction_q_2[5]), .FUNC4(Instruction_q_2[4]),
    .FUNC3(Instruction_q_2[3]), .FUNC2(Instruction_q_2[2]), .FUNC1(Instruction_q_2[1]),
    .FUNC0(Instruction_q_2[0]), .ALUOP3(alucontrol_1_shiftlocat[7]), .ALUOP2(alucontrol_1_shiftlocat[6]),
    .ALUOP1(alucontrol_1_shiftlocat[5]), .ALUOP0(alucontrol_1_shiftlocat[4]),
    .Choose2(alucontrol_1_shiftlocat[3]), .Choose1(alucontrol_1_shiftlocat[2]),
    .Choose0(alucontrol_1_shiftlocat[1]), .ShiftLocat(alucontrol_1_shiftlocat[0]));
  MainControl maincontrol_1 (
    .OP5(Instruction_q[5]), .OP4(Instruction_q[4]), .OP3(Instruction_q[3]), .OP2(Instruction_q[2]),
    .OP1(Instruction_q[1]), .OP0(Instruction_q[0]), .SignExtend(maincontrol_1_signextend),
    .RegDest(maincontrol_1_regdest[0]), .ALUsrc(maincontrol_1_regdest[1]),
    .MemRead(maincontrol_1_memread[0]), .MemW(maincontrol_1_memread[1]), .Branch(maincontrol_1_memread[2]),
    .MemToReg(maincontrol_1_memtoreg[0]), .RegWr(maincontrol_1_memtoreg[1]));
  LoadUse_Detector loaduse_detector_1 (
    .Is_load(and_1_out), .IF_ID_Ra(ID_Ra), .ID_EX_Rd(DXRd), .IF_ID_Rb(ID_Rb), .Is_LU_Hazard(LUH));
  not not_4 (not_4_out, Load_Store_EX_q[2]);
  Register #(.width(32)) register_1 (.D(multiplexer_9_out), .clk(c1_out), .Q(Instr));  // open: en, clr
  Multiplexer #(.width(32), .enable("false")) multiplexer_9 (
    .in0({Instruction_q, ID_Ra, ID_Rb, Instruction_q_4, Instruction_q_3, Instruction_q_2}),
    .in1(bit_extender_2_out), .out(multiplexer_9_out), .sel(LUH));
  assign bit_extender_6_out = {{31{1'b0}}, not_5_out};  // Bit_Extender bit_extender_6
  not not_5 (not_5_out, LUH);
  not not_6 (not_6_out, LUH);
  assign bit_extender_7_out = {{31{1'b0}}, not_6_out};  // Bit_Extender bit_extender_7
  Register #(.width(32)) PC4DE (
    .D(multiplexer_7_out), .clk(c1_out), .Q({PCabs[31:28], PC4DE_q, PC_8[1:0]}));  // open: en, clr
  Multiplexer #(.width(32), .enable("false")) multiplexer_10 (
    .in0(registerfile_1_p7), .in1(bit_extender_6_out), .out(multiplexer_10_out), .sel(LUH));
  Register #(.width(32)) A (.D(multiplexer_10_out), .clk(c1_out), .Q(A_q));  // open: en, clr
  Multiplexer #(.width(32), .enable("false")) multiplexer_11 (
    .in0(registerfile_1_p8), .in1(bit_extender_7_out), .out(multiplexer_11_out), .sel(LUH));
  assign bit_extender_8_out = {{31{1'b0}}, not_7_out};  // Bit_Extender bit_extender_8
  not not_7 (not_7_out, LUH);
  not not_8 (not_8_out, LUH);
  assign bit_extender_9_out = {{4{1'b0}}, not_8_out};  // Bit_Extender bit_extender_9
  not not_9 (not_9_out, LUH);
  assign bit_extender_10_out = {{4{1'b0}}, not_9_out};  // Bit_Extender bit_extender_10
  not not_10 (not_10_out, LUH);
  assign bit_extender_11_out = {{4{1'b0}}, not_10_out};  // Bit_Extender bit_extender_11
  not not_11 (not_11_out, LUH);
  assign bit_extender_12_out = {{4{1'b0}}, not_11_out};  // Bit_Extender bit_extender_12
  not not_12 (not_12_out, LUH);
  assign bit_extender_13_out = {{7{1'b0}}, not_12_out};  // Bit_Extender bit_extender_13
  not not_13 (not_13_out, LUH);
  assign bit_extender_14_out = {{1{1'b0}}, not_13_out};  // Bit_Extender bit_extender_14
  not not_14 (not_14_out, LUH);
  assign bit_extender_15_out = {{2{1'b0}}, not_14_out};  // Bit_Extender bit_extender_15
  assign bit_extender_16_out = {{1{1'b0}}, not_15_out};  // Bit_Extender bit_extender_16
  assign bit_extender_17_out = {{3{1'b0}}, not_16_out};  // Bit_Extender bit_extender_17
  Register #(.width(32)) B (.D(multiplexer_11_out), .clk(c1_out), .Q(B_q));  // open: en, clr
  Multiplexer #(.width(32), .enable("false")) multiplexer_12 (
    .in0(multiplexer_8_out), .in1(bit_extender_8_out), .out(multiplexer_12_out), .sel(LUH));
  Register #(.width(32)) Imm (.D(multiplexer_12_out), .clk(c1_out), .Q(Imm_q));  // open: en, clr
  Register #(.width(5)) Rd (.D(multiplexer_13_out), .clk(c1_out), .Q(Rd_q));  // open: en, clr
  Multiplexer #(.width(5), .enable("false")) multiplexer_13 (
    .in0(Instruction_q_4), .in1(bit_extender_9_out), .out(multiplexer_13_out), .sel(LUH));
  Register #(.width(5)) Rt (.D(multiplexer_14_out), .clk(c1_out), .Q(Rt_q));  // open: en, clr
  Multiplexer #(.width(5), .enable("false")) multiplexer_14 (
    .in0(ID_Rb), .in1(bit_extender_10_out), .out(multiplexer_14_out), .sel(LUH));
  Register #(.width(5)) Rs (.D(multiplexer_15_out), .clk(c1_out), .Q(Rs_q));  // open: en, clr
  Multiplexer #(.width(5), .enable("false")) multiplexer_15 (
    .in0(ID_Ra), .in1(bit_extender_11_out), .out(multiplexer_15_out), .sel(LUH));
  Register #(.width(5)) u_Sa (.D(multiplexer_16_out), .clk(c1_out), .Q(Sa_q));  // open: en, clr
  Multiplexer #(.width(5), .enable("false")) multiplexer_16 (
    .in0(Instruction_q_3), .in1(bit_extender_12_out), .out(multiplexer_16_out), .sel(LUH));
  Register ALUCtrl (.D(multiplexer_17_out), .clk(c1_out), .Q({ALUOP, Choose2, Choose10, ShiftLocat}));  // open: en, clr
  Multiplexer #(.width(8), .enable("false")) multiplexer_17 (
    .in0(alucontrol_1_shiftlocat), .in1(bit_extender_13_out), .out(multiplexer_17_out), .sel(LUH));
  Register #(.width(2)) EXCtrl (.D(multiplexer_18_out), .clk(c1_out), .Q(EXCtrl_q));  // open: en, clr
  Multiplexer #(.width(2), .enable("false")) multiplexer_18 (
    .in0(maincontrol_1_regdest), .in1(bit_extender_14_out), .out(multiplexer_18_out), .sel(LUH));
  Multiplexer #(.width(3), .enable("false")) multiplexer_19 (
    .in0(maincontrol_1_memread), .in1(bit_extender_15_out), .out(multiplexer_19_out), .sel(LUH));
  Multiplexer #(.width(2), .enable("false")) multiplexer_20 (
    .in0(maincontrol_1_memtoreg), .in1(bit_extender_16_out), .out(multiplexer_20_out), .sel(LUH));
  not not_15 (not_15_out, LUH);
  Multiplexer #(.width(4), .enable("false")) multiplexer_21 (
    .in0(load_storecontrol_1_ls0), .in1(bit_extender_17_out), .out(multiplexer_21_out), .sel(LUH));
  not not_16 (not_16_out, LUH);
  Register #(.width(3)) MEMCtrl0 (.D(multiplexer_19_out), .clk(c1_out), .Q(MEMCtrl0_q));  // open: en, clr
  Register #(.width(2)) WBCtrl0 (.D(multiplexer_20_out), .clk(c1_out), .Q(WBCtrl0_q));  // open: en, clr
  Register #(.width(4)) Load_Store_EX (
    .D(multiplexer_21_out), .clk(c1_out), .Q({Use_RAM, Load_Store_EX_q}));  // open: en, clr
  LeftShift2 leftshift2_1 (.Ins(Instr), .OutP({leftshift2_1_outp, PCabs[27:0]}));
  LeftShift2 leftshift2_2 (.Ins(Imm_q), .OutP(leftshift2_2_outp));
  Multiplexer #(.select(2), .width(32), .enable("false")) multiplexer_22 (
    .in0(A_q), .in1(WBdata), .in2(XMALU), .out(FrA), .sel(ForwA));  // open: in3
  Multiplexer #(.select(2), .width(32), .enable("false")) multiplexer_23 (
    .in0(B_q), .in1(WBdata), .in2(XMALU), .out(FrB), .sel(ForwB));  // open: in3
  Multiplexer #(.width(32), .enable("false")) multiplexer_24 (
    .in0(FrB), .in1(Imm_q), .out(multiplexer_24_out), .sel(EXCtrl_q[1]));
  Multiplexer #(.width(5), .enable("false")) multiplexer_25 (.in0(Rs_q), .in1(Sa_q), .out(SA), .sel(ShiftLocat));
  // Incrementer #(.width(30)) incrementer_2: pin names not known; wires that end beside it: {PCabs[31:28], PC4DE_q}, PC_8[31:2]
  // Mips_ALU mips_alu_1: pin names not known; wires that end beside it: FrA, multiplexer_24_out, ALUOP, SA, mips_alu_1_p5
  LUI lui_1 (.B(multiplexer_24_out), .Outp(lui_1_outp));
  Multiplexer #(.width(5), .enable("false")) multiplexer_26 (
    .in0(Rt_q), .in1(Rd_q), .out(multiplexer_26_out), .sel(EXCtrl_q[0]));
  SLT slt_1 (.A(FrA), .B(multiplexer_24_out), .UnOutp(slt_1_unoutp), .SiOupt(slt_1_sioupt));
  Multiplexer #(.width(32), .enable("false")) multiplexer_27 (
    .in0(slt_1_unoutp), .in1(slt_1_sioupt), .out(multiplexer_27_out), .sel(Choose2));
  MOVZ movz_1 (.rt(Rt_q), .rs_A(FrA), .Outp(movz_1_outp), .RegWr_Q(Q));
  and and_2 (and_2_out, ~Choose2, Q);  // AND_Gate
  and and_3 (and_3_out, ~Q, Choose2);  // AND_Gate
  and and_4 (and_4_out, Choose10[0], Choose10[1]);
  Adder #(.width(32)) adder_1 (
    .a(leftshift2_2_outp), .b({PCabs[31:28], PC4DE_q, PC_8[1:0]}), .out(PCrel));  // open: cin, cout
  Multiplexer #(.select(2), .width(32), .enable("false")) multiplexer_28 (
    .in0(mips_alu_1_p5), .in1(multiplexer_27_out), .in2(lui_1_outp), .in3(movz_1_outp),
    .out(multiplexer_28_out), .sel(Choose10));
  PCctrlDecode pcctrldecode_1 (
    .Instr(Instr), .JR(JR), .JAL(pcctrldecode_1_jal), .JAL_JALR(pcctrldecode_1_jal_jalr), .PCsel0(Jump),
    .PCsel1(PCsel[1]));
  BranchOrNot branchornot_1 (.Instr(Instr), .rA(FrA), .rB(FrB), .PCsel2(Branch));
  or or_2 (or_2_out, and_2_out, and_3_out);
  assign bit_extender_18_out = {{4{1'b1}}, pcctrldecode_1_jal};  // Bit_Extender bit_extender_18
  ForwardingUnit forwardingunit_1 (
    .XMRegW(XMRegW), .XMRd(XMRd), .DXRs(Rs_q), .DXRt(Rt_q), .MWRegW(RegWrite), .MWRd(RegDest),
    .ForwardA(ForwA), .ForwardB(ForwB));
  Multiplexer #(.enable("false")) multiplexer_29 (
    .in0(WBCtrl0_q[1]), .in1(multiplexer_30_out), .out(multiplexer_29_out), .sel(RI));
  Multiplexer #(.enable("false")) multiplexer_30 (
    .in0(WBCtrl0_q[1]), .in1(or_2_out), .out(multiplexer_30_out), .sel(and_4_out));
  not not_17 (not_17_out, JR);
  Calc_Store_Load calc_store_load_1 (
    .R_rs(FrA), .SignEXT_imm(Imm_q), .Load_Store_addr(calc_store_load_1_load_store_addr));
  not not_18 (not_18_out, Use_RAM);
  Multiplexer #(.width(5), .enable("false")) multiplexer_31 (
    .in0(multiplexer_26_out), .in1(bit_extender_18_out), .out(DXRd), .sel(pcctrldecode_1_jal));
  R_I_type r_i_type_1 (.Instr(Instr), .R_I_type(RI));
  Multiplexer #(.enable("false")) multiplexer_32 (
    .in0(multiplexer_29_out), .in1(not_17_out), .out(multiplexer_32_out[1]), .sel(JR));
  Multiplexer #(.width(32), .enable("false")) multiplexer_33 (
    .in0(calc_store_load_1_load_store_addr), .in1(multiplexer_28_out), .out(multiplexer_33_out),
    .sel(not_18_out));
  Register #(.width(32)) PCreg (.D(undriven), .clk(c1_out), .Q(PCreg_q));  // open: en, clr
  Register #(.width(32)) u_PCabs (.clk(c1_out), .Q(PCabs_q));  // open: D, en, clr
  Register #(.width(32)) ALUresultD (.D(multiplexer_34_out), .clk(c1_out), .Q(XMALU));  // open: en, clr
  Multiplexer #(.width(32), .enable("false")) multiplexer_34 (
    .in0(multiplexer_33_out), .in1(PC_8), .out(multiplexer_34_out), .sel(pcctrldecode_1_jal_jalr));
  Register #(.width(32)) MEM_B (.D(FrB), .clk(c1_out), .Q(MEM_B_q));  // open: en, clr
  Register #(.width(5)) Dest0 (.D(DXRd), .clk(c1_out), .Q(XMRd));  // open: en, clr
  Register #(.width(3)) u_PCsel (.clk(c1_out));  // open: D, en, Q, clr
  Register #(.width(3)) MEMCtrl1 (.D(MEMCtrl0_q), .clk(c1_out));  // open: en, Q, clr
  Register #(.width(2)) WBCtrl1 (
    .D({multiplexer_32_out[1], WBCtrl0_q[0]}), .clk(c1_out), .Q({XMRegW, XMMemToReg}));  // open: en, clr
  Register #(.width(4)) Load_Store_MEM (
    .D({Use_RAM, Load_Store_EX_q}), .clk(c1_out), .Q(Load_Store_MEM_q));  // open: en, clr
  Register #(.width(32)) u_PCrel (.clk(c1_out), .Q(PCrel_q));  // open: D, en, clr
  assign bit_extender_19_out = {{20{1'b0}}, XMALU[31:20]};  // Bit_Extender bit_extender_19
  // Probe on Load_Store_MEM_q
  // Probe on MEM_B_q
  // Probe on XMALU
  // Probe on XMALU[19:2]
  Decoder #(.select(2), .enable("false")) decoder_1 (
    .out0(decoder_1_out0[0]), .out1(decoder_1_out0[1]), .out2(decoder_1_out0[2]), .out3(decoder_1_out0[3]),
    .sel(XMALU[1:0]));
  assign bit_extender_20_out = {{3{1'b1}}, Load_Store_MEM_q[3]};  // Bit_Extender bit_extender_20
  Is_zero is_zero_1 (.in_1(bit_extender_19_out), .is_zero(is_zero_1_is_zero));
  // Probe on multiplexer_35_out
  Multiplexer #(.width(4), .enable("false")) multiplexer_35 (
    .in0(decoder_1_out0), .in1(bit_extender_20_out), .out(multiplexer_35_out), .sel(Load_Store_MEM_q[0]));
  and and_5 (and_5_out, Load_Store_MEM_q[3], Load_Store_MEM_q[2], is_zero_1_is_zero);
  and and_6 (and_6_out, Load_Store_MEM_q[3], not_19_out, is_zero_1_is_zero);
  not not_19 (not_19_out, Load_Store_MEM_q[2]);
  // MIPS_RAM #(.addrWidth(18)) mips_ram_1: pin names not known; wires that end beside it: XMALU[19:2], MEM_B_q, and_5_out, multiplexer_35_out, c1_out, and_6_out, mips_ram_1_p7
  Multiplexer #(.select(2), .width(8), .enable("false")) multiplexer_36 (
    .in0(mips_ram_1_p7[7:0]), .in1(mips_ram_1_p7[15:8]), .in2(mips_ram_1_p7[23:16]),
    .in3(mips_ram_1_p7[31:24]), .out(multiplexer_36_out), .sel(XMALU[1:0]));
  // Probe on multiplexer_36_out
  not not_20 (not_20_out, Load_Store_MEM_q[0]);
  not not_21 (not_21_out, Load_Store_MEM_q[2]);
  assign bit_extender_21_out = {{24{multiplexer_36_out[7]}}, multiplexer_36_out};  // Bit_Extender bit_extender_21
  Multiplexer #(.width(32), .enable("false")) multiplexer_37 (
    .in0(bit_extender_21_out), .in1(bit_extender_22_out), .out(multiplexer_37_out), .sel(and_7_out));
  assign bit_extender_22_out = {{24{1'b0}}, multiplexer_36_out};  // Bit_Extender bit_extender_22
  and and_7 (and_7_out, not_20_out, Load_Store_MEM_q[1], not_21_out, Load_Store_MEM_q[3]);
  Multiplexer #(.width(32), .enable("false")) multiplexer_38 (
    .in0(mips_ram_1_p7), .in1(multiplexer_37_out), .out(multiplexer_38_out), .sel(and_8_out));
  and and_8 (and_8_out, not_22_out, not_23_out, Load_Store_MEM_q[3]);
  not not_22 (not_22_out, Load_Store_MEM_q[0]);
  not not_23 (not_23_out, Load_Store_MEM_q[2]);
  Register #(.width(32)) ALUresult1 (.D(XMALU), .clk(c1_out), .Q(ALUresult1_q));  // open: en, clr
  Register #(.width(32)) MEMdata (.D(multiplexer_38_out), .clk(c1_out), .Q(MEMdata_q));  // open: en, clr
  Register #(.width(5)) Dest1 (.D(XMRd), .clk(c1_out), .Q(RegDest));  // open: en, clr
  Register #(.width(1)) RAM_or_not (.D(Load_Store_MEM_q[3]), .clk(c1_out), .Q(RAM_or_not_q));  // open: en, clr
  Register #(.width(2)) WBCtrl2 (.D({XMRegW, XMMemToReg}), .clk(c1_out), .Q({RegWrite, MemToReg}));  // open: en, clr
  // Probe on RAM_or_not_q
  Multiplexer #(.width(32), .enable("false")) multiplexer_39 (
    .in0(ALUresult1_q), .in1(MEMdata_q), .out(WBdata), .sel(RAM_or_not_q));
  // Probe on WBdata

  // Other names for the same wires on the sheet: PCreg[31:0] = FrA; PCsel (some bits) = {Branch, Jump}

  // Notes on the sheet:
  //   IF stage
  //   IF/ID
  //   contents of mipsprogramrom_1 (hex, n*v repeats v):
  //   ADDIU $a0, $zero, 1             # n = 3 (n in a0)       ADDIU $a1, $zero, 0             # log_arr
  //   starts at 1000 (n in a0)      ADDIU $a2, $zero, 3             # size = 3      ADDIU $sp, $sp, 1000
  //   # sp = 1000 (stack pointer initial to 1000)     JAL fib         NOP     J exit  #build DP table #
  //   ADDIU $t0, $t0, 4               # t0 = 4                SLL $t1, $s1, 2         # 4*size        SUBU
  //   $sp, $sp, $t1              # (1000 - 4*size) is the size for DP table    fib:       #prologue
  //   ADDIU $sp, $sp, -40     SW $ra, 36($sp)                 # save $ra      SW $fp, 32($sp)         #
  //   save old $fp  SW $a0, 28($sp)         # save n in callee saved s0     SW $a2, 24($sp)         # save
  //   size in callee saved s2  SW $a1, 20($sp)         # save log_arr pointer in callee saved s1
  //   #a0-a4:0 to 12; DP_pointer to 16; fib_result to 20      ADDIU $fp, $sp, 36      # set new frame ptr
  //   #Body #if(n < size)        SLT $t0, $a0, $a2               # if n < size   BEQ $t0, $zero, case1   #
  //   ( n > size, go to case2)      NOP     #log_array[n]   SLL $t1, $a0, 2         # 4*n   ADDU $t2, $t1,
  //   $a1      # log_array[n] = MEM(DP_pointer + offset)       LW  $t3, 0($t2)         # t3 = og_array[n]
  //   BEQ $zero, $t3, case1   # (log_array[n]==0, go to case2)        NOP     MOVZ $v0, $t3, $0       J
  //   epilogue                              #log_array[n]   NOP  # if (n==0) case1:         BNE $a0,
  //   $zero, case2   NOP     MOVZ $v0, $a0, $0       J epilogue                              #return 0
  //   NOP  # if (n==1) case2:         ADDIU $t6, $zero, 1             # t6 = 1 (for branch when n ==1)
  //   BNE $a0, $t6, fib_recurse       NOP     MOVZ $v0, $a0, $0       J epilogue
  //   #return 1               NOP  # loop fib_recurse:        #first function         ADDIU $a0, $a0, -1
  //   #n-1    JAL fib                 #recursion      NOP     LW $a0, 28($sp)         #restore n      SW
  //   $v0, 16($sp)         #save result of fib(n-1)        #second function        ADDIU $a0, $a0, -2
  //   #n-2    JAL fib                 #recursion      NOP     lW $t0, 16($sp)         #restore result of
  //   fib(n-1)     LW $a0, 28($sp)         #restore n      ADDU $v0,$t0,$v0                #calc result  #
  //   if (n < size)   SLT $t0, $a0, $a2               # if n < size   BEQ $t0, $zero, epilogue        # (
  //   n > size, go to epilogue)   NOP     #log_array[n]   SLL $t1, $a0, 2         # 4*n   ADDU $t2, $t1,
  //   $a1      # log_array[n] = MEM(DP_pointer + offset)       SW  $v0, 0($t2)         # log_array[n] =
  //   answer  epilogue:      LW $ra, 36($sp)                 # restore $ra   LW $fp, 32($sp)
  //   # restore fp    LW $a0, 28($sp)         # restore n in callee saved s0  LW $a1, 20($sp)         #
  //   save log_arr pointer in callee saved s1       LW $a2, 24($sp)         # restore size in callee saved
  //   s1       ADDIU $sp, $sp, 40              #dealloc frame  JR $ra  NOP exit:
  //   ID stage
  //   ID/EX
  //   EX stage
  //   Except JALR
  //   EX/MEM
  //   byte-aligned mem
  //   word/byte
  //   MEM stage
  //   LB/LBU
  //   LW/LB,LBU
  //   MEM/WB
  //   RAM or not
  //   WB stage
endmodule

module MainControl (
  input  OP5,
  input  OP4,
  input  OP3,
  input  OP2,
  input  OP1,
  input  OP0,
  output SignExtend,
  output RegDest,
  output ALUsrc,
  output MemRead,
  output MemW,
  output Branch,
  output MemToReg,
  output RegWr
);

  wire and_2_out, and_6_out, and_7_out, and_8_out, and_9_out, and_10_out, not_1_out, not_2_out, not_3_out,
       not_4_out, not_5_out, not_6_out, not_7_out, not_8_out, not_9_out, not_10_out, not_11_out, not_12_out,
       not_13_out, not_14_out, not_15_out, not_16_out, not_17_out, not_18_out;

  not not_1 (not_1_out, OP4);
  not not_2 (not_2_out, OP3);
  not not_3 (not_3_out, OP5);
  not not_4 (not_4_out, OP3);
  or or_1 (ALUsrc, OP3, OP5);
  not not_5 (not_5_out, OP3);
  and and_1 (MemW, OP5, OP3);
  not not_6 (not_6_out, OP5);
  not not_7 (not_7_out, OP3);
  not not_8 (not_8_out, OP3);
  not not_9 (not_9_out, OP2);
  not not_10 (not_10_out, OP1);
  not not_11 (not_11_out, OP0);
  not not_12 (not_12_out, OP3);
  not not_13 (not_13_out, OP2);
  not not_14 (not_14_out, OP5);
  not not_15 (not_15_out, OP3);
  not not_16 (not_16_out, OP2);
  not not_17 (not_17_out, OP3);
  and and_2 (and_2_out, not_1_out, not_2_out);
  not not_18 (not_18_out, OP2);
  and and_3 (RegDest, not_3_out, not_4_out);
  and and_4 (MemRead, OP5, not_5_out);
  and and_5 (Branch, not_6_out, not_7_out, OP2);
  and and_6 (and_6_out, not_8_out, not_9_out, not_10_out, not_11_out);
  and and_7 (and_7_out, not_12_out, not_13_out, OP1, OP0);
  and and_8 (and_8_out, not_14_out, OP3);
  and and_9 (and_9_out, OP4, not_15_out, not_16_out);
  and and_10 (and_10_out, OP5, not_17_out);
  or or_2 (SignExtend, and_2_out, not_18_out, OP5);
  or or_3 (RegWr, and_6_out, and_7_out, and_8_out, and_9_out, and_10_out);

  assign MemToReg = OP5;
endmodule

module LUI (
  input  [31:0] B,
  output [31:0] Outp
);


  assign Outp = {B[15:0], B[31:16]};
endmodule

module MOVZ (
  input  [4:0] rt,
  input  [31:0] rs_A,
  output [31:0] Outp,
  output RegWr_Q
);

  wire [4:0] not_1_out;

  assign not_1_out = ~rt;  // NOT_Gate not_1, 5 bits wide
  and and_1 (RegWr_Q, not_1_out[0], not_1_out[1], not_1_out[2], not_1_out[3], not_1_out[4]);

  assign Outp = rs_A;
endmodule

module ALUControl (
  input  OP5,
  input  OP4,
  input  OP3,
  input  OP2,
  input  OP1,
  input  OP0,
  input  FUNC5,
  input  FUNC4,
  input  FUNC3,
  input  FUNC2,
  input  FUNC1,
  input  FUNC0,
  output ALUOP3,
  output ALUOP2,
  output ALUOP1,
  output ALUOP0,
  output Choose2,
  output Choose1,
  output Choose0,
  output ShiftLocat
);

  wire and_1_out, and_2_out, and_3_out, and_4_out, and_5_out, and_6_out, and_7_out, and_8_out, and_9_out,
       and_10_out, and_11_out, and_12_out, and_13_out, and_14_out, and_15_out, and_16_out, and_17_out,
       and_18_out, and_19_out, and_20_out, and_21_out, and_22_out, and_23_out, and_24_out, and_25_out,
       not_1_out, not_2_out, not_3_out, not_4_out, not_5_out, not_6_out, not_7_out, not_8_out, not_9_out,
       not_10_out, not_11_out, not_12_out, not_13_out, not_14_out, not_15_out, not_16_out, not_17_out,
       not_18_out, not_19_out, not_20_out, not_21_out, not_22_out, not_23_out, not_24_out, not_25_out,
       not_26_out, not_27_out, not_28_out, not_29_out, not_30_out, not_31_out, not_32_out, not_33_out,
       not_34_out, not_35_out, not_36_out, not_37_out;

  not not_1 (not_1_out, OP0);
  not not_2 (not_2_out, FUNC5);
  not not_3 (not_3_out, FUNC3);
  not not_4 (not_4_out, FUNC0);
  not not_5 (not_5_out, OP3);
  not not_6 (not_6_out, OP1);
  not not_7 (not_7_out, OP5);
  not not_8 (not_8_out, OP4);
  not not_9 (not_9_out, OP3);
  not not_10 (not_10_out, OP5);
  not not_11 (not_11_out, OP4);
  not not_12 (not_12_out, OP0);
  not not_13 (not_13_out, OP1);
  and and_1 (and_1_out, not_13_out, FUNC5, FUNC0);
  not not_14 (not_14_out, OP3);
  and and_2 (and_2_out, not_14_out, OP1);
  not not_15 (not_15_out, OP2);
  and and_3 (and_3_out, not_15_out, OP1);
  and and_4 (and_4_out, OP4, OP1);
  and and_5 (and_5_out, OP5, OP1);
  not not_16 (not_16_out, OP3);
  and and_6 (and_6_out, not_16_out, not_17_out, FUNC0);
  not not_17 (not_17_out, FUNC5);
  not not_18 (not_18_out, OP3);
  and and_7 (and_7_out, not_18_out, OP1);
  not not_19 (not_19_out, OP2);
  and and_8 (and_8_out, not_19_out, OP1);
  and and_9 (and_9_out, OP1, OP0);
  and and_10 (and_10_out, OP4, OP1);
  and and_11 (and_11_out, OP5, OP1);
  not not_20 (not_20_out, OP3);
  not not_21 (not_21_out, FUNC5);
  not not_22 (not_22_out, OP5);
  not not_23 (not_23_out, OP4);
  not not_24 (not_24_out, OP3);
  not not_25 (not_25_out, OP2);
  not not_26 (not_26_out, OP1);
  not not_27 (not_27_out, OP0);
  not not_28 (not_28_out, FUNC4);
  not not_29 (not_29_out, FUNC2);
  not not_30 (not_30_out, OP5);
  not not_31 (not_31_out, OP4);
  not not_32 (not_32_out, OP2);
  not not_33 (not_33_out, OP0);
  not not_34 (not_34_out, OP3);
  and and_12 (and_12_out, not_34_out, not_35_out, FUNC3);
  not not_35 (not_35_out, FUNC5);
  and and_13 (and_13_out, OP2, OP1, OP0);
  not not_36 (not_36_out, OP3);
  and and_14 (and_14_out, not_36_out, FUNC3);
  not not_37 (not_37_out, OP2);
  and and_15 (and_15_out, not_37_out, OP1);
  not not_38 (ShiftLocat, FUNC2);
  and and_16 (and_16_out, not_1_out, not_2_out, FUNC4, not_3_out, FUNC2, FUNC1, not_4_out);
  and and_17 (and_17_out, not_5_out, FUNC5, FUNC2);
  and and_18 (and_18_out, OP2, not_6_out);
  and and_19 (and_19_out, OP2, OP0);
  and and_20 (and_20_out, not_7_out, not_8_out, OP3, OP2);
  and and_21 (and_21_out, not_9_out, FUNC1);
  and and_22 (and_22_out, not_10_out, not_11_out, OP3, OP2, OP1, not_12_out);
  and and_23 (and_23_out, not_20_out, not_21_out, FUNC3, FUNC0);
  and and_24 (and_24_out, not_22_out, not_23_out, not_24_out, not_25_out, not_26_out, not_27_out, not_28_out, FUNC3, not_29_out, FUNC1, FUNC0);
  and and_25 (and_25_out, not_30_out, not_31_out, OP3, not_32_out, OP1, not_33_out);
  or or_1 (Choose1, and_12_out, and_13_out);
  or or_2 (Choose0, and_14_out, and_15_out);
  or or_3 (ALUOP3, and_16_out, and_17_out, and_18_out, and_19_out, and_20_out);
  or or_4 (ALUOP2, and_21_out, and_22_out);
  or or_5 (ALUOP1, and_1_out, OP0, and_2_out, and_3_out, and_4_out, and_5_out);
  or or_6 (ALUOP0, and_6_out, and_7_out, and_8_out, and_9_out, and_10_out, and_11_out);
  or or_7 (Choose2, and_23_out, and_24_out, and_25_out);
endmodule

module SLT (
  input  [31:0] A,
  input  [31:0] B,
  output [31:0] UnOutp,
  output [31:0] SiOupt
);

  wire comparator_1_lt, comparator_2_lt;

  Comparator #(.width(32), .mode("unsigned")) comparator_1 (.a(A), .b(B), .lt(comparator_1_lt));  // open: gt, eq
  Comparator #(.width(32)) comparator_2 (.a(A), .b(B), .lt(comparator_2_lt));  // open: gt, eq
  assign UnOutp = {{31{1'b0}}, comparator_1_lt};  // Bit_Extender bit_extender_1
  assign SiOupt = {{31{1'b0}}, comparator_2_lt};  // Bit_Extender bit_extender_2

  // Notes on the sheet:
  //   Unsigned_A<B?
  //   Signed_A<B?
endmodule

module Detect_B_Instr (
  input  [31:0] Origin_Instr,
  output [31:0] No_B_Instr
);

  wire and_1_out, and_2_out, nand_1_out, not_1_out, or_1_out;
  wire [31:0] bit_extender_1_out;

  and and_1 (and_1_out, ~Origin_Instr[1], ~Origin_Instr[2], Origin_Instr[3], ~Origin_Instr[4], ~Origin_Instr[5], ~Origin_Instr[26], ~Origin_Instr[27], ~Origin_Instr[28], ~Origin_Instr[29], ~Origin_Instr[30], ~Origin_Instr[31]);  // AND_Gate
  not not_1 (not_1_out, or_1_out);
  nand nand_1 (nand_1_out, ~Origin_Instr[26], ~Origin_Instr[27], ~Origin_Instr[28]);  // NAND_Gate
  and and_2 (and_2_out, nand_1_out, ~Origin_Instr[29], ~Origin_Instr[30], ~Origin_Instr[31]);  // AND_Gate
  assign bit_extender_1_out = {{31{1'b0}}, not_1_out};  // Bit_Extender bit_extender_1
  or or_1 (or_1_out, and_2_out, and_1_out, Origin_Instr[31]);
  Multiplexer #(.width(32), .enable("false")) multiplexer_1 (
    .in0(Origin_Instr), .in1(bit_extender_1_out), .out(No_B_Instr), .sel(or_1_out));
endmodule

module ForwardingChoose (
  input  case1,
  input  case2,
  input  case3,
  input  case4,
  output A1,
  output A0,
  output B1,
  output B0
);

  wire not_1_out, not_2_out;

  not not_1 (not_1_out, case1);
  and and_1 (A0, not_1_out, case3);
  not not_2 (not_2_out, case2);
  and and_2 (B0, not_2_out, case4);

  assign A1 = case1;
  assign B1 = case2;
endmodule

module ForwardingUnit (
  input  XMRegW,
  input  [4:0] XMRd,
  input  [4:0] DXRs,
  input  [4:0] DXRt,
  input  MWRegW,
  input  [4:0] MWRd,
  output [1:0] ForwardA,
  output [1:0] ForwardB
);

  wire and_1_out, and_2_out, and_3_out, and_4_out, and_5_out, and_6_out, nor_1_out, nor_2_out, nor_3_out,
       nor_4_out, not_1_out, not_2_out, or_1_out, or_2_out;
  wire [4:0] xor_1_out, xor_2_out, xor_3_out, xor_4_out;

  or or_1 (or_1_out, XMRd[0], XMRd[1], XMRd[2], XMRd[3], XMRd[4]);
  assign xor_1_out = XMRd ^ DXRs;  // XOR_Gate xor_1, 5 bits wide
  assign xor_2_out = XMRd ^ DXRt;  // XOR_Gate xor_2, 5 bits wide
  assign xor_3_out = DXRs ^ MWRd;  // XOR_Gate xor_3, 5 bits wide
  assign xor_4_out = DXRt ^ MWRd;  // XOR_Gate xor_4, 5 bits wide
  nor nor_1 (nor_1_out, xor_1_out[0], xor_1_out[1], xor_1_out[2], xor_1_out[3], xor_1_out[4]);
  nor nor_2 (nor_2_out, xor_2_out[0], xor_2_out[1], xor_2_out[2], xor_2_out[3], xor_2_out[4]);
  nor nor_3 (nor_3_out, xor_3_out[0], xor_3_out[1], xor_3_out[2], xor_3_out[3], xor_3_out[4]);
  or or_2 (or_2_out, MWRd[0], MWRd[1], MWRd[2], MWRd[3], MWRd[4]);
  nor nor_4 (nor_4_out, xor_4_out[0], xor_4_out[1], xor_4_out[2], xor_4_out[3], xor_4_out[4]);
  and and_1 (and_1_out, XMRegW, or_1_out, nor_1_out);
  and and_2 (and_2_out, XMRegW, or_1_out, nor_2_out);
  not not_1 (not_1_out, and_1_out);
  not not_2 (not_2_out, and_2_out);
  and and_3 (and_3_out, XMRegW, or_1_out, nor_1_out);
  and and_4 (and_4_out, XMRegW, or_1_out, nor_2_out);
  and and_5 (and_5_out, nor_3_out, not_1_out, MWRegW, or_2_out);
  and and_6 (and_6_out, nor_4_out, not_2_out, or_2_out, MWRegW);
  ForwardingChoose forwardingchoose_1 (
    .case1(and_3_out), .case2(and_4_out), .case3(and_5_out), .case4(and_6_out), .A1(ForwardA[1]),
    .A0(ForwardA[0]), .B1(ForwardB[1]), .B0(ForwardB[0]));

  // Notes on the sheet:
  //   EX Hazard 1
  //   EX Hazard 2
  //   MEM 1
  //   MEM 2
endmodule

module LeftShift2 (
  input  [31:0] Ins,
  output [31:0] OutP
);

  wire not_1_out;

  not not_1 (not_1_out, Ins[0]);
  and and_1 (OutP[1], not_1_out, Ins[0]);

  assign {OutP[31:2], OutP[0]} = {Ins[29:0], OutP[1]};
endmodule

module PCctrlDecode (
  input  [31:0] Instr,
  output JR,
  output JAL,
  output JAL_JALR,
  output PCsel0,
  output PCsel1
);

  wire and_2_out, and_4_out;

  and and_1 (JAL, Instr[26], Instr[27], ~Instr[28], ~Instr[29], ~Instr[30], ~Instr[31]);  // AND_Gate
  and and_2 (and_2_out, ~Instr[26], Instr[27], ~Instr[28], ~Instr[29], ~Instr[30], ~Instr[31]);  // AND_Gate
  and and_3 (JR, ~Instr[0], ~Instr[1], ~Instr[2], Instr[3], ~Instr[4], ~Instr[5], ~Instr[26], ~Instr[27], ~Instr[28], ~Instr[29], ~Instr[30], ~Instr[31]);  // AND_Gate
  and and_4 (and_4_out, Instr[0], ~Instr[1], ~Instr[2], Instr[3], ~Instr[4], ~Instr[5], ~Instr[26], ~Instr[27], ~Instr[28], ~Instr[29], ~Instr[30], ~Instr[31]);  // AND_Gate
  or or_1 (JAL_JALR, and_4_out, JAL);
  or or_2 (PCsel0, JR, and_4_out, and_2_out, JAL);
  or or_3 (PCsel1, JAL, and_2_out);

  // Notes on the sheet:
  //   J
  //   JR
  //   JALR
  //   JAL
  //   PCreg/PCabs
  //   JR/JALR/J/JAL
  //   PCabs
  //   J/JAL
endmodule

module BranchOrNot (
  input  [31:0] Instr,
  input  [31:0] rA,
  input  [31:0] rB,
  output PCsel2
);

  wire and_3_out, and_4_out, and_5_out, and_6_out, and_7_out, and_8_out, and_9_out, c, comparator_1_gt,
       comparator_1_lt, comparator_2_eq, Eq, IsBranchInstr, multiplexer_1_out, multiplexer_2_out,
       multiplexer_3_out, multiplexer_4_out, multiplexer_5_out, not_1_out, not_2_out, not_3_out, not_4_out;
  wire [31:0] bit_extender_1_out;

  not not_1 (not_1_out, rA[0]);
  and and_1 (Eq, ~Instr[27], Instr[28]);  // AND_Gate
  and and_2 (c, Instr[27], Instr[28]);
  Comparator #(.width(32)) comparator_1 (
    .a(rA), .b(bit_extender_1_out), .gt(comparator_1_gt), .lt(comparator_1_lt));  // open: eq
  and and_3 (and_3_out, rA[0], not_1_out);
  Comparator #(.width(32)) comparator_2 (.a(rA), .b(rB), .eq(comparator_2_eq));  // open: gt, lt
  assign bit_extender_1_out = {{31{1'b0}}, and_3_out};  // Bit_Extender bit_extender_1
  not not_2 (not_2_out, comparator_2_eq);
  not not_3 (not_3_out, comparator_1_gt);
  Multiplexer #(.enable("false")) multiplexer_1 (
    .in0(not_3_out), .in1(comparator_1_gt), .out(multiplexer_1_out), .sel(Instr[26]));
  not not_4 (not_4_out, comparator_1_lt);
  Multiplexer #(.enable("false")) multiplexer_2 (
    .in0(multiplexer_3_out), .in1(multiplexer_1_out), .out(multiplexer_2_out), .sel(c));
  Multiplexer #(.enable("false")) multiplexer_3 (
    .in0(comparator_1_lt), .in1(not_4_out), .out(multiplexer_3_out), .sel(Instr[16]));
  Multiplexer #(.enable("false")) multiplexer_4 (
    .in0(comparator_2_eq), .in1(not_2_out), .out(multiplexer_4_out), .sel(Instr[26]));
  Multiplexer #(.enable("false")) multiplexer_5 (
    .in0(multiplexer_2_out), .in1(multiplexer_4_out), .out(multiplexer_5_out), .sel(Eq));
  Multiplexer #(.enable("false")) multiplexer_6 (
    .in0(IsBranchInstr), .in1(multiplexer_5_out), .out(PCsel2), .sel(IsBranchInstr));
  and and_4 (and_4_out, ~Instr[26], ~Instr[27], Instr[28], ~Instr[29], ~Instr[30], ~Instr[31]);  // AND_Gate
  and and_5 (and_5_out, Instr[26], ~Instr[27], Instr[28], ~Instr[29], ~Instr[30], ~Instr[31]);  // AND_Gate
  and and_6 (and_6_out, ~Instr[26], Instr[27], Instr[28], ~Instr[29], ~Instr[30], ~Instr[31]);  // AND_Gate
  and and_7 (and_7_out, Instr[26], Instr[27], Instr[28], ~Instr[29], ~Instr[30], ~Instr[31]);  // AND_Gate
  and and_8 (and_8_out, ~Instr[16], ~Instr[17], ~Instr[18], ~Instr[19], ~Instr[20], Instr[26], ~Instr[27], ~Instr[28], ~Instr[29], ~Instr[30], ~Instr[31]);  // AND_Gate
  and and_9 (and_9_out, Instr[16], ~Instr[17], ~Instr[18], ~Instr[19], ~Instr[20], Instr[26], ~Instr[27], ~Instr[28], ~Instr[29], ~Instr[30], ~Instr[31]);  // AND_Gate
  or or_1 (IsBranchInstr, and_4_out, and_5_out, and_6_out, and_7_out, and_8_out, and_9_out);

  // Other names for the same wires on the sheet: Sr0 = Instr[16]; Op0 = Instr[26]
endmodule

module Load_storeControl (
  input  OP5,
  input  OP4,
  input  OP3,
  input  OP2,
  input  OP1,
  input  OP0,
  output LS0,
  output LS1,
  output LS2,
  output LS3
);

  wire and_1_out, and_2_out, and_3_out, not_1_out, not_2_out, not_3_out, not_4_out, not_5_out, not_6_out,
       not_7_out, not_8_out, not_9_out, not_10_out;

  not not_1 (not_1_out, OP4);
  not not_2 (not_2_out, OP3);
  not not_3 (not_3_out, OP1);
  not not_4 (not_4_out, OP0);
  not not_5 (not_5_out, OP4);
  not not_6 (not_6_out, OP2);
  not not_7 (not_7_out, OP1);
  not not_8 (not_8_out, OP0);
  not not_9 (not_9_out, OP4);
  not not_10 (not_10_out, OP2);
  and and_1 (and_1_out, OP5, not_1_out, not_2_out, not_3_out, not_4_out);
  and and_2 (and_2_out, OP5, not_5_out, not_6_out, not_7_out, not_8_out);
  and and_3 (and_3_out, OP5, not_9_out, not_10_out, OP1, OP0);
  or or_1 (LS3, and_1_out, and_2_out, and_3_out);

  assign LS0 = OP1;
  assign LS1 = OP2;
  assign LS2 = OP3;
endmodule

module Is_zero (
  input  [31:0] in_1,
  output is_zero
);

  nor nor_1 (is_zero, in_1[15], in_1[0], in_1[1], in_1[2], in_1[3], in_1[4], in_1[5], in_1[6], in_1[7], in_1[8], in_1[9], in_1[10], in_1[11], in_1[12], in_1[13], in_1[14], in_1[16], in_1[17], in_1[18], in_1[19], in_1[20], in_1[21], in_1[22], in_1[23], in_1[24], in_1[25], in_1[26], in_1[27], in_1[28], in_1[29], in_1[30], in_1[31]);
endmodule

module Calc_Store_Load (
  input  [31:0] R_rs,
  input  [31:0] SignEXT_imm,
  output [31:0] Load_Store_addr
);

  Adder #(.width(32)) adder_1 (.a(R_rs), .b(SignEXT_imm), .out(Load_Store_addr));  // open: cin, cout
endmodule

module R_I_type (
  input  [31:0] Instr,
  output R_I_type
);

  wire and_1_out, and_2_out, and_3_out, or_1_out;

  and and_1 (and_1_out, ~Instr[26], ~Instr[27], ~Instr[28], Instr[29], ~Instr[30], ~Instr[31]);  // AND_Gate
  and and_2 (and_2_out, ~Instr[26], ~Instr[27], ~Instr[28], ~Instr[29], ~Instr[30], ~Instr[31]);  // AND_Gate
  and and_3 (and_3_out, Instr[0], ~Instr[1], ~Instr[2], Instr[3], ~Instr[4], ~Instr[5], ~Instr[26], ~Instr[27], ~Instr[28], ~Instr[29], ~Instr[30], ~Instr[31]);  // AND_Gate
  or or_1 (or_1_out, and_1_out, and_2_out);
  and and_4 (R_I_type, ~and_3_out, or_1_out);  // AND_Gate
endmodule

module LoadUse_Detector (
  input  Is_load,
  input  [4:0] IF_ID_Ra,
  input  [4:0] ID_EX_Rd,
  input  [4:0] IF_ID_Rb,
  output Is_LU_Hazard
);

  wire and_1_out, and_2_out, or_1_out, or_2_out;
  wire [4:0] xnor_1_out, xnor_2_out;

  assign xnor_1_out = ~(IF_ID_Ra ^ ID_EX_Rd);  // XNOR_Gate xnor_1, 5 bits wide
  assign xnor_2_out = ~(ID_EX_Rd ^ IF_ID_Rb);  // XNOR_Gate xnor_2, 5 bits wide
  and and_1 (and_1_out, xnor_1_out[0], xnor_1_out[1], xnor_1_out[2], xnor_1_out[3], xnor_1_out[4]);
  and and_2 (and_2_out, xnor_2_out[0], xnor_2_out[1], xnor_2_out[2], xnor_2_out[3], xnor_2_out[4]);
  or or_1 (or_1_out, ID_EX_Rd[0], ID_EX_Rd[1], ID_EX_Rd[2], ID_EX_Rd[3], ID_EX_Rd[4]);
  or or_2 (or_2_out, and_1_out, and_2_out);
  and and_3 (Is_LU_Hazard, Is_load, or_1_out, or_2_out);
endmodule
